// Logisim project S1-T18-DES-Logisim-Final.circ as structural Verilog: 6 circuits, main circuit Overall
module Overall (
  input  [7:0] Plaintext___Ciphertext,
  input  E_D,
  input  [9:0] KEY,
  output [7:0] Ciphertext___Plaintext
);

  wire C_out, comparator_1_gt, comparator_2_gt, comparator_3_gt, comparator_4_gt, comparator_5_gt,
       comparator_5_lt, demultiplexer_1_out1, demultiplexer_2_out1, demultiplexer_3_out1,
       demultiplexer_4_out1, demultiplexer_5_out1, demultiplexer_6_out1, R_out;
  wire [3:0] n4_bit_swap_1_out_l, n4_bit_swap_1_out_r, round_1_f0, round_1_f4, round_2_f0, round_2_f4;
  wire [5:0] counter_1_q;
  wire [7:0] initial_permutation_1_out, key_1_key1, key_1_key2;

  Button C (.out(C_out));
  Button R (.out(R_out));
  Counter #(.width(6), .max('h3f), .ongoal("continue")) counter_1 (
    .count(1'b1), .Q(counter_1_q), .clk(C_out), .clr(R_out));  // open: load, D, carry
  Comparator #(.width(6), .mode("unsigned")) comparator_1 (
    .a(counter_1_q), .b(6'b001011), .gt(comparator_1_gt));  // open: eq, lt
  Comparator #(.width(6), .mode("unsigned")) comparator_2 (
    .a(counter_1_q), .b(6'b010101), .gt(comparator_2_gt));  // open: eq, lt
  Comparator #(.width(6), .mode("unsigned")) comparator_3 (
    .a(counter_1_q), .b(6'b011010), .gt(comparator_3_gt));  // open: eq, lt
  Comparator #(.width(6), .mode("unsigned")) comparator_4 (
    .a(counter_1_q), .b(6'b011111), .gt(comparator_4_gt));  // open: eq, lt
  Demultiplexer demultiplexer_1 (.out1(demultiplexer_1_out1), .in(C_out), .sel(comparator_1_gt));  // open: out0, en
  Demultiplexer demultiplexer_2 (.out1(demultiplexer_2_out1), .in(C_out), .sel(comparator_2_gt));  // open: out0, en
  Demultiplexer demultiplexer_3 (.out1(demultiplexer_3_out1), .in(C_out), .sel(comparator_3_gt));  // open: out0, en
  Demultiplexer demultiplexer_4 (.out1(demultiplexer_4_out1), .in(C_out), .sel(comparator_4_gt));  // open: out0, en
  INITIAL_PERMUTATION initial_permutation_1 (
    .add_car(1'b0), .reg_en(1'b1), .in(Plaintext___Ciphertext), .comp_1(4'b1000), .clk_data(1'b1),
    .Clk(demultiplexer_1_out1), .Reset(R_out), .comp_2(4'b0001), .out(initial_permutation_1_out));
  Round round_1 (
    .add_car(1'b0), .reg_en(1'b1), .comp_1(3'b100), .clk_data(1'b1), .Clk(demultiplexer_2_out1),
    .Reset(R_out), .comp_2(4'b0001), .a(initial_permutation_1_out[7]), .b(initial_permutation_1_out[6]),
    .c(initial_permutation_1_out[5]), .d(initial_permutation_1_out[4]), .e(initial_permutation_1_out[3]),
    .f(initial_permutation_1_out[2]), .g(initial_permutation_1_out[1]), .h(initial_permutation_1_out[0]),
    .i(key_1_key1[7]), .j(key_1_key1[6]), .k(key_1_key1[5]), .l(key_1_key1[4]), .m(key_1_key1[3]),
    .n(key_1_key1[2]), .o(key_1_key1[1]), .p(key_1_key1[0]), .f0(round_1_f0[0]), .f1(round_1_f0[1]),
    .f2(round_1_f0[2]), .f3(round_1_f0[3]), .f4(round_1_f4[0]), .f5(round_1_f4[1]), .f6(round_1_f4[2]),
    .f7(round_1_f4[3]));
  _4___BIT_SWAP u_4_bit_swap_1 (
    .r4(round_1_f0), .l4(round_1_f4), .out_r(n4_bit_swap_1_out_r), .out_l(n4_bit_swap_1_out_l));
  Round round_2 (
    .add_car(1'b0), .reg_en(1'b1), .comp_1(3'b100), .clk_data(1'b1), .Clk(demultiplexer_3_out1),
    .Reset(R_out), .comp_2(4'b0001), .a(n4_bit_swap_1_out_l[3]), .b(n4_bit_swap_1_out_l[2]),
    .c(n4_bit_swap_1_out_l[1]), .d(n4_bit_swap_1_out_l[0]), .e(n4_bit_swap_1_out_r[3]),
    .f(n4_bit_swap_1_out_r[2]), .g(n4_bit_swap_1_out_r[1]), .h(n4_bit_swap_1_out_r[0]), .i(key_1_key2[7]),
    .j(key_1_key2[6]), .k(key_1_key2[5]), .l(key_1_key2[4]), .m(key_1_key2[3]), .n(key_1_key2[2]),
    .o(key_1_key2[1]), .p(key_1_key2[0]), .f0(round_2_f0[0]), .f1(round_2_f0[1]), .f2(round_2_f0[2]),
    .f3(round_2_f0[3]), .f4(round_2_f4[0]), .f5(round_2_f4[1]), .f6(round_2_f4[2]), .f7(round_2_f4[3]));
  INVERSE_INITIAL_PERMUTATION inverse_initial_permutation_1 (
    .add_carry(1'b0), .reg_en(1'b1), .in({round_2_f4, round_2_f0}), .comp_1(4'b1000), .clk_data(1'b1),
    .Clk(demultiplexer_4_out1), .Reset(R_out), .comp_2(4'b0001), .out(Ciphertext___Plaintext));
  Key key_1 (
    .add3_car(1'b0), .reg3_en(1'b1), .add1_carry(1'b0), .reg1_en(1'b1), .comp6(4'b1000), .clock3_data(1'b1),
    .\input (KEY), .add2_car(1'b0), .Clk_3(demultiplexer_5_out1), .reg2_en(1'b1), .comp2(4'b1010),
    .clock1_data(1'b1), .comp5(4'b0001), .Clk_1(demultiplexer_6_out1), .comp4(4'b1000), .clock2_data(1'b1),
    .comp1(4'b0001), .Clk_2(demultiplexer_5_out1), .comp3(4'b0001), .Reset(R_out), .en_de(E_D),
    .key1(key_1_key1), .key2(key_1_key2));
  Comparator #(.width(6), .mode("unsigned")) comparator_5 (
    .a(counter_1_q), .b(6'b001011), .gt(comparator_5_gt), .lt(comparator_5_lt));  // open: eq
  Demultiplexer demultiplexer_5 (.out1(demultiplexer_5_out1), .in(C_out), .sel(comparator_5_gt));  // open: out0, en
  Demultiplexer demultiplexer_6 (.out1(demultiplexer_6_out1), .in(C_out), .sel(comparator_5_lt));  // open: out0, en

  // Notes on the sheet:
  //   Clock
  //   Reset
  //   Encryption / Decryption
  //   SMALL SCALE IMPLEMENTATION OF DES ALGORITHM 
  //   OVERALL CIRCUIT
  //   1. Click on the "Reset" button to reset the circuit. 
  //   3. For encryption, set E/D to 0. For decryption, set it to 1.
  //   4. Click on the "Clock" button for at least 40 times. 
  //   INSTRUCTIONS
  //   5. The desired output (ciphertext for encryption and plaintexxt for decryption) will appear in the "Output" box.
  //   2. Enter the values of the plaintext (for encryption) or ciphertext (for decryption) (under input) and key (under key).
endmodule

module Key (
  input  add3_car,
  input  reg3_en,
  input  add1_carry,
  input  reg1_en,
  input  [3:0] comp6,
  input  clock3_data,
  input  [9:0] \input ,
  input  add2_car,
  input  Clk_3,
  input  reg2_en,
  input  [3:0] comp2,
  input  clock1_data,
  input  [3:0] comp5,
  input  Clk_1,
  input  Reset,
  input  [3:0] comp4,
  input  clock2_data,
  input  [3:0] comp1,
  input  Clk_2,
  input  [3:0] comp3,
  input  en_de,
  output [7:0] key1,
  output [7:0] key2
);

  wire and_1_out, and_2_out, and_3_out, bitselector_1_out, bitselector_2_out, bitselector_3_out,
       comparator_1_eq, comparator_1_lt, comparator_2_eq, comparator_2_gt, comparator_3_eq, comparator_3_lt,
       comparator_4_eq, comparator_4_gt, comparator_5_eq, comparator_5_lt, comparator_6_eq, comparator_6_gt,
       not_1_out, not_2_out, not_3_out, or_1_out, or_2_out, or_3_out;
  wire [3:0] counter_1_q, counter_2_q, counter_3_q, counter_4_q, counter_5_q, counter_6_q,
       demultiplexer_2_out1, demultiplexer_6_out1, demultiplexer_10_out1;
  wire [4:0] demultiplexer_4_out1, demultiplexer_4_out1_2;
  wire [7:0] adder_2_out, adder_3_out, demultiplexer_5_out1, demultiplexer_7_out1, demultiplexer_8_out1,
       demultiplexer_9_out1, demultiplexer_11_out1, demultiplexer_12_out1, register_2_q, register_3_q;
  wire [9:0] adder_1_out, demultiplexer_1_out4, demultiplexer_3_out1, register_1_q;

  Counter #(.width(4), .max('hf), .ongoal("continue")) counter_1 (
    .count(clock1_data), .Q(counter_1_q), .clk(Clk_1), .clr(Reset));  // open: load, D, carry
  Comparator #(.width(4), .mode("unsigned")) comparator_1 (
    .a(counter_1_q), .b(comp2), .eq(comparator_1_eq), .lt(comparator_1_lt));  // open: gt
  BitSelector #(.width(10)) bitselector_1 (.in(\input ), .out(bitselector_1_out), .sel(demultiplexer_2_out1));
  Demultiplexer #(.select(4)) demultiplexer_1 (
    .out0(demultiplexer_1_out4[4]), .out1(demultiplexer_1_out4[2]), .out2(demultiplexer_1_out4[1]),
    .out3(demultiplexer_1_out4[6]), .out4(demultiplexer_1_out4[0]), .out5(demultiplexer_1_out4[8]),
    .out6(demultiplexer_1_out4[5]), .out7(demultiplexer_1_out4[9]), .out8(demultiplexer_1_out4[7]),
    .out9(demultiplexer_1_out4[3]), .in(bitselector_1_out), .sel(demultiplexer_2_out1));  // open: out10, out11, out12, out13, out14, out15, en
  Demultiplexer #(.width(4), .enable("false")) demultiplexer_2 (
    .out1(demultiplexer_2_out1), .in(counter_1_q), .sel(comparator_1_lt));  // open: out0
  Counter #(.width(4), .max('hf), .ongoal("continue")) counter_2 (
    .count(comparator_1_eq), .Q(counter_2_q), .clk(Clk_1), .clr(Reset));  // open: load, D, carry
  Comparator #(.width(4), .mode("unsigned")) comparator_2 (
    .a(counter_2_q), .b(comp1), .gt(comparator_2_gt), .eq(comparator_2_eq));  // open: lt
  not not_1 (not_1_out, or_1_out);
  or or_1 (or_1_out, comparator_2_gt, comparator_2_eq);
  and and_1 (and_1_out, comparator_1_lt, not_1_out);
  Adder #(.width(10)) adder_1 (
    .a(demultiplexer_1_out4), .b(demultiplexer_3_out1), .out(adder_1_out), .cin(add1_carry));  // open: cout
  Demultiplexer #(.width(10)) demultiplexer_3 (
    .out1(demultiplexer_3_out1), .in(register_1_q), .sel(and_1_out), .en(and_1_out));  // open: out0
  Register #(.width(10)) register_1 (.D(adder_1_out), .en(reg1_en), .Q(register_1_q), .clk(Clk_1), .clr(Reset));
  Demultiplexer #(.width(10)) demultiplexer_4 (
    .out1({demultiplexer_4_out1_2[0], demultiplexer_4_out1_2[4:1], demultiplexer_4_out1[0], demultiplexer_4_out1[4:1]}),
    .in(register_1_q), .sel(or_1_out), .en(or_1_out));  // open: out0
  Counter #(.width(4), .max('hf), .ongoal("continue")) counter_3 (
    .count(clock2_data), .Q(counter_3_q), .clk(Clk_2), .clr(Reset));  // open: load, D, carry
  BitSelector #(.width(10)) bitselector_2 (
    .in({demultiplexer_4_out1_2, demultiplexer_4_out1}), .out(bitselector_2_out), .sel(demultiplexer_6_out1));
  Demultiplexer #(.select(4)) demultiplexer_5 (
    .out0(demultiplexer_5_out1[1]), .out1(demultiplexer_5_out1[0]), .out2(demultiplexer_5_out1[3]),
    .out3(demultiplexer_5_out1[5]), .out4(demultiplexer_5_out1[7]), .out5(demultiplexer_5_out1[2]),
    .out6(demultiplexer_5_out1[4]), .out7(demultiplexer_5_out1[6]), .in(bitselector_2_out),
    .sel(demultiplexer_6_out1));  // open: out8, out9, out10, out11, out12, out13, out14, out15, en
  Demultiplexer #(.width(4), .enable("false")) demultiplexer_6 (
    .out1(demultiplexer_6_out1), .in(counter_3_q), .sel(comparator_3_lt));  // open: out0
  Comparator #(.width(4), .mode("unsigned")) comparator_3 (
    .a(counter_3_q), .b(comp4), .eq(comparator_3_eq), .lt(comparator_3_lt));  // open: gt
  Counter #(.width(4), .max('hf), .ongoal("continue")) counter_4 (
    .count(comparator_3_eq), .Q(counter_4_q), .clk(Clk_2), .clr(Reset));  // open: load, D, carry
  Comparator #(.width(4), .mode("unsigned")) comparator_4 (
    .a(counter_4_q), .b(comp3), .gt(comparator_4_gt), .eq(comparator_4_eq));  // open: lt
  not not_2 (not_2_out, or_2_out);
  or or_2 (or_2_out, comparator_4_gt, comparator_4_eq);
  and and_2 (and_2_out, comparator_3_lt, not_2_out);
  Adder adder_2 (.a(demultiplexer_5_out1), .b(demultiplexer_7_out1), .out(adder_2_out), .cin(add2_car));  // open: cout
  Demultiplexer #(.width(8)) demultiplexer_7 (
    .out1(demultiplexer_7_out1), .in(register_2_q), .sel(and_2_out), .en(and_2_out));  // open: out0
  Register register_2 (.D(adder_2_out), .en(reg2_en), .Q(register_2_q), .clk(Clk_2), .clr(Reset));
  Demultiplexer #(.width(8)) demultiplexer_8 (
    .out1(demultiplexer_8_out1), .in(register_2_q), .sel(or_2_out), .en(or_2_out));  // open: out0
  Counter #(.width(4), .max('hf), .ongoal("continue")) counter_5 (
    .count(clock3_data), .Q(counter_5_q), .clk(Clk_3), .clr(Reset));  // open: load, D, carry
  BitSelector #(.width(10)) bitselector_3 (
    .in({demultiplexer_4_out1_2[2:0], demultiplexer_4_out1_2[4:3], demultiplexer_4_out1[2:0], demultiplexer_4_out1[4:3]}),
    .out(bitselector_3_out), .sel(demultiplexer_10_out1));
  Demultiplexer #(.select(4)) demultiplexer_9 (
    .out0(demultiplexer_9_out1[1]), .out1(demultiplexer_9_out1[0]), .out2(demultiplexer_9_out1[3]),
    .out3(demultiplexer_9_out1[5]), .out4(demultiplexer_9_out1[7]), .out5(demultiplexer_9_out1[2]),
    .out6(demultiplexer_9_out1[4]), .out7(demultiplexer_9_out1[6]), .in(bitselector_3_out),
    .sel(demultiplexer_10_out1));  // open: out8, out9, out10, out11, out12, out13, out14, out15, en
  Demultiplexer #(.width(4), .enable("false")) demultiplexer_10 (
    .out1(demultiplexer_10_out1), .in(counter_5_q), .sel(comparator_5_lt));  // open: out0
  Comparator #(.width(4), .mode("unsigned")) comparator_5 (
    .a(counter_5_q), .b(comp6), .eq(comparator_5_eq), .lt(comparator_5_lt));  // open: gt
  Counter #(.width(4), .max('hf), .ongoal("continue")) counter_6 (
    .count(comparator_5_eq), .Q(counter_6_q), .clk(Clk_3), .clr(Reset));  // open: load, D, carry
  Comparator #(.width(4), .mode("unsigned")) comparator_6 (
    .a(counter_6_q), .b(comp5), .gt(comparator_6_gt), .eq(comparator_6_eq));  // open: lt
  not not_3 (not_3_out, or_3_out);
  or or_3 (or_3_out, comparator_6_gt, comparator_6_eq);
  and and_3 (and_3_out, comparator_5_lt, not_3_out);
  Multiplexer #(.width(8)) multiplexer_1 (
    .in0(demultiplexer_12_out1), .in1(demultiplexer_8_out1), .out(key2), .sel(en_de));  // open: en
  Adder adder_3 (.a(demultiplexer_9_out1), .b(demultiplexer_11_out1), .out(adder_3_out), .cin(add3_car));  // open: cout
  Demultiplexer #(.width(8)) demultiplexer_11 (
    .out1(demultiplexer_11_out1), .in(register_3_q), .sel(and_3_out), .en(and_3_out));  // open: out0
  Multiplexer #(.width(8)) multiplexer_2 (
    .in0(demultiplexer_8_out1), .in1(demultiplexer_12_out1), .out(key1), .sel(en_de));  // open: en
  Register register_3 (.D(adder_3_out), .en(reg3_en), .Q(register_3_q), .clk(Clk_3), .clr(Reset));
  Demultiplexer #(.width(8)) demultiplexer_12 (
    .out1(demultiplexer_12_out1), .in(register_3_q), .sel(or_3_out), .en(or_3_out));  // open: out0

  // Notes on the sheet:
  //   KEY
endmodule

// IP
module INITIAL_PERMUTATION (
  input  add_car,
  input  reg_en,
  input  [7:0] in,
  input  [3:0] comp_1,
  input  clk_data,
  input  Clk,
  input  Reset,
  input  [3:0] comp_2,
  output [7:0] out
);

  wire and_1_out, bitselector_1_out, comparator_1_eq, comparator_1_lt, comparator_2_eq, comparator_2_gt,
       not_1_out, or_1_out;
  wire [2:0] demultiplexer_2_out1;
  wire [3:0] counter_1_q, counter_2_q;
  wire [3:3] demultiplexer_2_out1_2;
  wire [7:0] adder_1_out, demultiplexer_1_out1, demultiplexer_3_out1, register_1_q;

  Counter #(.width(4), .max('hf), .ongoal("continue")) counter_1 (
    .count(clk_data), .Q(counter_1_q), .clk(Clk), .clr(Reset));  // open: load, D, carry
  BitSelector bitselector_1 (.in(in), .out(bitselector_1_out), .sel(demultiplexer_2_out1));
  Comparator #(.width(4), .mode("unsigned")) comparator_1 (
    .a(counter_1_q), .b(comp_1), .eq(comparator_1_eq), .lt(comparator_1_lt));  // open: gt
  Counter #(.width(4), .max('hf), .ongoal("continue")) counter_2 (
    .count(comparator_1_eq), .Q(counter_2_q), .clk(Clk), .clr(Reset));  // open: load, D, carry
  Demultiplexer #(.select(3)) demultiplexer_1 (
    .out0(demultiplexer_1_out1[2]), .out1(demultiplexer_1_out1[0]), .out2(demultiplexer_1_out1[6]),
    .out3(demultiplexer_1_out1[1]), .out4(demultiplexer_1_out1[3]), .out5(demultiplexer_1_out1[5]),
    .out6(demultiplexer_1_out1[7]), .out7(demultiplexer_1_out1[4]), .in(bitselector_1_out),
    .sel(demultiplexer_2_out1));  // open: en
  Demultiplexer #(.width(4), .enable("false")) demultiplexer_2 (
    .out1({demultiplexer_2_out1_2[3], demultiplexer_2_out1}), .in(counter_1_q), .sel(comparator_1_lt));  // open: out0
  not not_1 (not_1_out, or_1_out);
  Comparator #(.width(4), .mode("unsigned")) comparator_2 (
    .a(counter_2_q), .b(comp_2), .gt(comparator_2_gt), .eq(comparator_2_eq));  // open: lt
  or or_1 (or_1_out, comparator_2_gt, comparator_2_eq);
  and and_1 (and_1_out, comparator_1_lt, not_1_out);
  Adder adder_1 (.a(demultiplexer_1_out1), .b(demultiplexer_3_out1), .out(adder_1_out), .cin(add_car));  // open: cout
  Demultiplexer #(.width(8)) demultiplexer_3 (
    .out1(demultiplexer_3_out1), .in(register_1_q), .sel(and_1_out), .en(and_1_out));  // open: out0
  Register register_1 (.D(adder_1_out), .en(reg_en), .Q(register_1_q), .clk(Clk), .clr(Reset));
  Demultiplexer #(.width(8)) demultiplexer_4 (
    .out1(out), .in(register_1_q), .sel(or_1_out), .en(or_1_out));  // open: out0

  // Notes on the sheet:
  //   INITIAL PERMUTATION
endmodule

// Round
module Round (
  input  a,
  input  b,
  input  c,
  input  d,
  input  e,
  input  f,
  input  g,
  input  h,
  input  i,
  input  j,
  input  k,
  input  l,
  input  m,
  input  n,
  input  o,
  input  p,
  input  add_car,
  input  reg_en,
  input  [2:0] comp_1,
  input  clk_data,
  input  Clk,
  input  Reset,
  input  [3:0] comp_2,
  output f0,
  output f1,
  output f2,
  output f3,
  output f4,
  output f5,
  output f6,
  output f7
);

  wire and_1_out, and_2_out, and_3_out, and_4_out, and_5_out, and_6_out, and_7_out, and_8_out, and_9_out,
       and_10_out, and_11_out, and_12_out, and_13_out, and_14_out, and_15_out, bitselector_1_out,
       comparator_1_eq, comparator_1_lt, comparator_2_eq, comparator_2_gt, not_1_out, not_2_out, not_3_out,
       not_4_out, not_5_out, not_6_out, not_7_out, not_8_out, not_9_out, or_1_out, or_3_out, or_6_out,
       xnor_1_out, xnor_2_out, xor_1_out, xor_2_out, xor_3_out, xor_4_out, xor_5_out, xor_6_out, xor_7_out,
       xor_8_out, xor_9_out, xor_10_out;
  wire [1:0] demultiplexer_2_out1;
  wire [2:0] counter_1_q;
  wire [2:2] demultiplexer_2_out1_2;
  wire [3:0] adder_1_out, counter_2_q, demultiplexer_1_out3, demultiplexer_3_out1, demultiplexer_4_out1,
       or_7_out, register_1_q;

  not not_1 (not_1_out, xor_2_out);
  and and_1 (and_1_out, not_1_out, not_3_out, xor_7_out);
  not not_2 (not_2_out, xor_3_out);
  not not_3 (not_3_out, xor_4_out);
  or or_1 (or_1_out, xor_3_out, xor_7_out);
  and and_2 (and_2_out, not_1_out, xor_4_out, not_2_out, not_4_out);
  not not_4 (not_4_out, xor_7_out);
  xor xor_1 (xor_1_out, xor_3_out, xor_7_out);
  and and_3 (and_3_out, xor_2_out, xor_1_out);
  or or_2 (or_7_out[3], and_1_out, and_2_out, and_3_out, and_4_out, and_5_out);
  and and_4 (and_4_out, xor_4_out, xor_3_out, not_4_out);
  and and_5 (and_5_out, xor_2_out, xor_4_out, or_1_out);
  xor xor_2 (xor_2_out, h, i);
  or or_3 (or_3_out, xor_7_out, not_1_out, xor_4_out);
  and and_6 (and_6_out, not_2_out, or_3_out);
  or or_4 (or_7_out[2], and_6_out, and_7_out);
  xor xor_3 (xor_3_out, f, k);
  xor xor_4 (xor_4_out, e, j);
  xor xor_5 (xor_5_out, xor_7_out, xor_4_out);
  and and_7 (and_7_out, xor_2_out, xor_5_out);
  xor xor_6 (xor_6_out, f, m);
  xor xor_7 (xor_7_out, g, l);
  xor xor_8 (xor_8_out, g, n);
  xor xor_9 (xor_9_out, h, o);
  xor xor_10 (xor_10_out, e, p);
  and and_8 (and_8_out, xor_6_out, not_7_out, not_8_out);
  Counter #(.width(3), .max('h7), .ongoal("continue")) counter_1 (
    .count(clk_data), .Q(counter_1_q), .clk(Clk), .clr(Reset));  // open: load, D, carry
  and and_9 (and_9_out, xor_10_out, xnor_1_out);
  and and_10 (and_10_out, not_5_out, xor_8_out, xor_9_out);
  or or_5 (or_7_out[1], and_8_out, and_10_out, and_9_out, and_11_out);
  BitSelector #(.width(4)) bitselector_1 (.in(or_7_out), .out(bitselector_1_out), .sel(demultiplexer_2_out1));
  Comparator #(.width(3), .mode("unsigned")) comparator_1 (
    .a(counter_1_q), .b(comp_1), .eq(comparator_1_eq), .lt(comparator_1_lt));  // open: gt
  Counter #(.width(4), .max('hf), .ongoal("continue")) counter_2 (
    .count(comparator_1_eq), .Q(counter_2_q), .clk(Clk), .clr(Reset));  // open: load, D, carry
  not not_5 (not_5_out, xor_6_out);
  and and_11 (and_11_out, not_5_out, xor_8_out, not_9_out);
  Demultiplexer #(.select(2)) demultiplexer_1 (
    .out0(demultiplexer_1_out3[2]), .out1(demultiplexer_1_out3[1]), .out2(demultiplexer_1_out3[3]),
    .out3(demultiplexer_1_out3[0]), .in(bitselector_1_out), .sel(demultiplexer_2_out1));  // open: en
  Demultiplexer #(.width(3), .enable("false")) demultiplexer_2 (
    .out1({demultiplexer_2_out1_2[2], demultiplexer_2_out1}), .in(counter_1_q), .sel(comparator_1_lt));  // open: out0
  not not_6 (not_6_out, or_6_out);
  Comparator #(.width(4), .mode("unsigned")) comparator_2 (
    .a(counter_2_q), .b(comp_2), .gt(comparator_2_gt), .eq(comparator_2_eq));  // open: lt
  not not_7 (not_7_out, xor_8_out);
  xnor xnor_1 (xnor_1_out, xor_8_out, xor_9_out);
  or or_6 (or_6_out, comparator_2_gt, comparator_2_eq);
  not not_8 (not_8_out, xor_9_out);
  xnor xnor_2 (xnor_2_out, xor_9_out, xor_10_out);
  and and_12 (and_12_out, not_5_out, xor_9_out, not_9_out);
  and and_13 (and_13_out, comparator_1_lt, not_6_out);
  not not_9 (not_9_out, xor_10_out);
  and and_14 (and_14_out, not_5_out, xor_8_out, xor_10_out);
  or or_7 (or_7_out[0], and_12_out, and_14_out, and_15_out);
  and and_15 (and_15_out, xor_6_out, xnor_2_out);
  Adder #(.width(4)) adder_1 (
    .a(demultiplexer_1_out3), .b(demultiplexer_3_out1), .out(adder_1_out), .cin(add_car));  // open: cout
  Demultiplexer #(.width(4)) demultiplexer_3 (
    .out1(demultiplexer_3_out1), .in(register_1_q), .sel(and_13_out), .en(and_13_out));  // open: out0
  Register #(.width(4)) register_1 (.D(adder_1_out), .en(reg_en), .Q(register_1_q), .clk(Clk), .clr(Reset));
  Demultiplexer #(.width(4)) demultiplexer_4 (
    .out1(demultiplexer_4_out1), .in(register_1_q), .sel(or_6_out), .en(or_6_out));  // open: out0
  xor xor_11 (f4, demultiplexer_4_out1[0], d);
  xor xor_12 (f5, demultiplexer_4_out1[1], c);
  xor xor_13 (f6, demultiplexer_4_out1[2], b);
  xor xor_14 (f7, demultiplexer_4_out1[3], a);

  assign f0 = h;
  assign f1 = g;
  assign f2 = f;
  assign f3 = e;

  // Notes on the sheet:
  //   AFTER IP
  //   S0
  //   KEY
  //   TRANSPOSITION (P-BOX)
  //   EP
  //   XOR
  //   ROUND FUNCTION
  //   S1
  //   L-R XOR
endmodule

// SWAP
module _4___BIT_SWAP (
  input  [3:0] r4,
  input  [3:0] l4,
  output [3:0] out_r,
  output [3:0] out_l
);


  assign out_l = r4;
  assign out_r = l4;

  // Notes on the sheet:
  //   4 - BIT SWAP
endmodule

// IIP
module INVERSE_INITIAL_PERMUTATION (
  input  add_carry,
  input  reg_en,
  input  [7:0] in,
  input  [3:0] comp_1,
  input  clk_data,
  input  Clk,
  input  Reset,
  input  [3:0] comp_2,
  output [7:0] out
);

  wire and_1_out, bitselector_1_out, comparator_1_eq, comparator_1_lt, comparator_2_eq, comparator_2_gt,
       not_1_out, or_1_out;
  wire [2:0] demultiplexer_2_out1;
  wire [3:0] counter_1_q, counter_2_q;
  wire [3:3] demultiplexer_2_out1_2;
  wire [7:0] adder_1_out, demultiplexer_1_out2, demultiplexer_3_out1, register_1_q;

  Counter #(.width(4), .max('hf), .ongoal("continue")) counter_1 (
    .count(clk_data), .Q(counter_1_q), .clk(Clk), .clr(Reset));  // open: load, D, carry
  BitSelector bitselector_1 (.in(in), .out(bitselector_1_out), .sel(demultiplexer_2_out1));
  Comparator #(.width(4), .mode("unsigned")) comparator_1 (
    .a(counter_1_q), .b(comp_1), .eq(comparator_1_eq), .lt(comparator_1_lt));  // open: gt
  Counter #(.width(4), .max('hf), .ongoal("continue")) counter_2 (
    .count(comparator_1_eq), .Q(counter_2_q), .clk(Clk), .clr(Reset));  // open: load, D, carry
  Demultiplexer #(.select(3)) demultiplexer_1 (
    .out0(demultiplexer_1_out2[1]), .out1(demultiplexer_1_out2[3]), .out2(demultiplexer_1_out2[0]),
    .out3(demultiplexer_1_out2[4]), .out4(demultiplexer_1_out2[7]), .out5(demultiplexer_1_out2[5]),
    .out6(demultiplexer_1_out2[2]), .out7(demultiplexer_1_out2[6]), .in(bitselector_1_out),
    .sel(demultiplexer_2_out1));  // open: en
  Demultiplexer #(.width(4), .enable("false")) demultiplexer_2 (
    .out1({demultiplexer_2_out1_2[3], demultiplexer_2_out1}), .in(counter_1_q), .sel(comparator_1_lt));  // open: out0
  not not_1 (not_1_out, or_1_out);
  Comparator #(.width(4), .mode("unsigned")) comparator_2 (
    .a(counter_2_q), .b(comp_2), .gt(comparator_2_gt), .eq(comparator_2_eq));  // open: lt
  or or_1 (or_1_out, comparator_2_gt, comparator_2_eq);
  and and_1 (and_1_out, comparator_1_lt, not_1_out);
  Adder adder_1 (.a(demultiplexer_1_out2), .b(demultiplexer_3_out1), .out(adder_1_out), .cin(add_carry));  // open: cout
  Demultiplexer #(.width(8)) demultiplexer_3 (
    .out1(demultiplexer_3_out1), .in(register_1_q), .sel(and_1_out), .en(and_1_out));  // open: out0
  Register register_1 (.D(adder_1_out), .en(reg_en), .Q(register_1_q), .clk(Clk), .clr(Reset));
  Demultiplexer #(.width(8)) demultiplexer_4 (
    .out1(out), .in(register_1_q), .sel(or_1_out), .en(or_1_out));  // open: out0

  // Notes on the sheet:
  //   INVERSE INITIAL PERMUTATION
endmodule
